# Fritzing sketch Street Light Controller (saved by Fritzing 0.9.3b)
breadboards: 1

parts:
  Part1 = Arduino Nano (Rev3.0)
  R1 = Photocell (LDR) [package=THT]
  R2 = Resistor [tolerance=±5% resistance=1k package="0805 [SMD]"]
  R3 = Resistor [tolerance=±5% resistance=1k package="0805 [SMD]"]
  HC-SR04_Sensor_1 = HC-SR04 Ultrasonic Distance Sensor
  Mod1 = KY-015 Temperature & Humidity Sensor Module [package="Breakout board"]
  LED1 = smd LED [color="White (4500K)" package="0603 [SMD]"]

nets:
  GND: Part1.GND, R2.Pin_0, HC-SR04_Sensor_1.GND, Mod1.-, LED1.cathode
  N1: Part1.D2, R3.Pin_1
  N2: Part1.D4, Mod1.S
  N3: Part1.D10, HC-SR04_Sensor_1.TRIG
  N4: Part1.D11/MOSI, HC-SR04_Sensor_1.ECHO
  5V: Part1.5V, Part1.A6, R1.pin_0, HC-SR04_Sensor_1.VCC, Mod1.Vin
  N5: Part1.A3, Part1.A0, R1.pin_1, R2.Pin_1
  N6: R3.Pin_0, LED1.anode

custom parts:
  KY-015 Temperature & Humidity Sensor Module: KY-015 temperature and humidity sensor module, provides a low-latency serial interface to measure humidity and temperature.
